// Logisim project mobeius.circ as structural Verilog: 1 circuit, main circuit main
module main (
);

  wire clk, invert, output1, output2, output3, output4;

  D_Flip_Flop #(.trigger("falling")) d_ff_1 (.D(invert), .clk(clk), .Q(output1));  // open: Qn, preset, reset
  LED led_1 (.in(output4));
  D_Flip_Flop #(.trigger("falling")) d_ff_2 (.D(output1), .clk(clk), .Q(output2));  // open: Qn, preset, reset
  LED led_2 (.in(output3));
  D_Flip_Flop #(.trigger("falling")) d_ff_3 (.D(output2), .clk(clk), .Q(output3));  // open: Qn, preset, reset
  LED led_3 (.in(output2));
  D_Flip_Flop #(.trigger("falling")) d_ff_4 (.D(output3), .clk(clk), .Q(output4), .Qn(invert));  // open: preset, reset
  LED led_4 (.in(output1));
  Clock clock_1 (.out(clk));
endmodule
